// Logisim project memory_game.circ as structural Verilog
module main (
  input  in_1
);

  wire button_1_out;
  wire [4:0] single_display_1_out_2, single_display_1_out_3, single_display_1_out_4, single_display_1_out_5,
       single_display_1_out_6, single_display_2_out_2, single_display_2_out_3, single_display_2_out_4,
       single_display_2_out_5, single_display_2_out_6, single_display_3_out_2, single_display_3_out_3,
       single_display_3_out_4, single_display_3_out_5, single_display_3_out_6, single_display_4_out_2,
       single_display_4_out_3, single_display_4_out_4, single_display_4_out_5, single_display_4_out_6,
       single_display_5_out_2, single_display_5_out_3, single_display_5_out_4, single_display_5_out_5,
       single_display_5_out_6, single_display_mirrored_1_out_2, single_display_mirrored_1_out_3,
       single_display_mirrored_1_out_4, single_display_mirrored_1_out_5, single_display_mirrored_1_out_6,
       single_display_mirrored_2_out_2, single_display_mirrored_2_out_3, single_display_mirrored_2_out_4,
       single_display_mirrored_2_out_5, single_display_mirrored_2_out_6, single_display_mirrored_3_out_2,
       single_display_mirrored_3_out_3, single_display_mirrored_3_out_4, single_display_mirrored_3_out_5,
       single_display_mirrored_3_out_6, single_display_mirrored_4_out_2, single_display_mirrored_4_out_3,
       single_display_mirrored_4_out_4, single_display_mirrored_4_out_5, single_display_mirrored_4_out_6,
       single_display_mirrored_5_out_2, single_display_mirrored_5_out_3, single_display_mirrored_5_out_4,
       single_display_mirrored_5_out_5, single_display_mirrored_5_out_6;
  wire [8:0] d0, d1, d2, d3, d4, d5, d6, d7, d8, d9;

  Clock clock_1 ();  // open: out
  Button button_1 (.out(button_1_out));
  Hex_Digit_Display hex_digit_display_1 ();  // open: value, dp
  Hex_Digit_Display hex_digit_display_2 ();  // open: value, dp
  single_display single_display_1 (
    .in_1(d0), .out_2(single_display_1_out_2), .out_3(single_display_1_out_3),
    .out_4(single_display_1_out_4), .out_5(single_display_1_out_5), .out_6(single_display_1_out_6));
  DotMatrix #(.matrixrows(5)) dotmatrix_1 (
    .col0(single_display_1_out_6), .col1(single_display_1_out_5), .col2(single_display_1_out_4),
    .col3(single_display_1_out_3), .col4(single_display_1_out_2));
  DotMatrix #(.matrixrows(5)) dotmatrix_2 (
    .col0(single_display_2_out_6), .col1(single_display_2_out_5), .col2(single_display_2_out_4),
    .col3(single_display_2_out_3), .col4(single_display_2_out_2));
  DotMatrix #(.matrixrows(5)) dotmatrix_3 (
    .col0(single_display_mirrored_1_out_2), .col1(single_display_mirrored_1_out_3),
    .col2(single_display_mirrored_1_out_4), .col3(single_display_mirrored_1_out_5),
    .col4(single_display_mirrored_1_out_6));
  DotMatrix #(.matrixrows(5)) dotmatrix_4 (
    .col0(single_display_mirrored_2_out_2), .col1(single_display_mirrored_2_out_3),
    .col2(single_display_mirrored_2_out_4), .col3(single_display_mirrored_2_out_5),
    .col4(single_display_mirrored_2_out_6));
  single_display_mirrored single_display_mirrored_1 (
    .in_1(d1), .out_2(single_display_mirrored_1_out_2), .out_3(single_display_mirrored_1_out_3),
    .out_4(single_display_mirrored_1_out_4), .out_5(single_display_mirrored_1_out_5),
    .out_6(single_display_mirrored_1_out_6));
  single_display_mirrored single_display_mirrored_2 (
    .in_1(d3), .out_2(single_display_mirrored_2_out_2), .out_3(single_display_mirrored_2_out_3),
    .out_4(single_display_mirrored_2_out_4), .out_5(single_display_mirrored_2_out_5),
    .out_6(single_display_mirrored_2_out_6));
  Button button_2 ();  // open: out
  Button button_3 ();  // open: out
  single_display single_display_2 (
    .in_1(d2), .out_2(single_display_2_out_2), .out_3(single_display_2_out_3),
    .out_4(single_display_2_out_4), .out_5(single_display_2_out_5), .out_6(single_display_2_out_6));
  DotMatrix #(.matrixrows(5)) dotmatrix_5 (
    .col0(single_display_3_out_6), .col1(single_display_3_out_5), .col2(single_display_3_out_4),
    .col3(single_display_3_out_3), .col4(single_display_3_out_2));
  DotMatrix #(.matrixrows(5)) dotmatrix_6 (
    .col0(single_display_mirrored_3_out_2), .col1(single_display_mirrored_3_out_3),
    .col2(single_display_mirrored_3_out_4), .col3(single_display_mirrored_3_out_5),
    .col4(single_display_mirrored_3_out_6));
  single_display_mirrored single_display_mirrored_3 (
    .in_1(d5), .out_2(single_display_mirrored_3_out_2), .out_3(single_display_mirrored_3_out_3),
    .out_4(single_display_mirrored_3_out_4), .out_5(single_display_mirrored_3_out_5),
    .out_6(single_display_mirrored_3_out_6));
  Button button_4 ();  // open: out
  Button button_5 ();  // open: out
  Button button_6 ();  // open: out
  Button button_7 ();  // open: out
  Hex_Digit_Display hex_digit_display_3 ();  // open: value, dp
  single_display single_display_3 (
    .in_1(d4), .out_2(single_display_3_out_2), .out_3(single_display_3_out_3),
    .out_4(single_display_3_out_4), .out_5(single_display_3_out_5), .out_6(single_display_3_out_6));
  single_display single_display_4 (
    .in_1(d6), .out_2(single_display_4_out_2), .out_3(single_display_4_out_3),
    .out_4(single_display_4_out_4), .out_5(single_display_4_out_5), .out_6(single_display_4_out_6));
  DotMatrix #(.matrixrows(5)) dotmatrix_7 (
    .col0(single_display_4_out_6), .col1(single_display_4_out_5), .col2(single_display_4_out_4),
    .col3(single_display_4_out_3), .col4(single_display_4_out_2));
  DotMatrix #(.matrixrows(5)) dotmatrix_8 (
    .col0(single_display_mirrored_4_out_2), .col1(single_display_mirrored_4_out_3),
    .col2(single_display_mirrored_4_out_4), .col3(single_display_mirrored_4_out_5),
    .col4(single_display_mirrored_4_out_6));
  single_display_mirrored single_display_mirrored_4 (
    .in_1(d7), .out_2(single_display_mirrored_4_out_2), .out_3(single_display_mirrored_4_out_3),
    .out_4(single_display_mirrored_4_out_4), .out_5(single_display_mirrored_4_out_5),
    .out_6(single_display_mirrored_4_out_6));
  Button button_8 ();  // open: out
  Button button_9 ();  // open: out
  Button button_10 ();  // open: out
  Button button_11 ();  // open: out
  Hex_Digit_Display hex_digit_display_4 ();  // open: value, dp
  single_display single_display_5 (
    .in_1(d8), .out_2(single_display_5_out_2), .out_3(single_display_5_out_3),
    .out_4(single_display_5_out_4), .out_5(single_display_5_out_5), .out_6(single_display_5_out_6));
  DotMatrix #(.matrixrows(5)) dotmatrix_9 (
    .col0(single_display_5_out_6), .col1(single_display_5_out_5), .col2(single_display_5_out_4),
    .col3(single_display_5_out_3), .col4(single_display_5_out_2));
  DotMatrix #(.matrixrows(5)) dotmatrix_10 (
    .col0(single_display_mirrored_5_out_2), .col1(single_display_mirrored_5_out_3),
    .col2(single_display_mirrored_5_out_4), .col3(single_display_mirrored_5_out_5),
    .col4(single_display_mirrored_5_out_6));
  single_display_mirrored single_display_mirrored_5 (
    .in_1(d9), .out_2(single_display_mirrored_5_out_2), .out_3(single_display_mirrored_5_out_3),
    .out_4(single_display_mirrored_5_out_4), .out_5(single_display_mirrored_5_out_5),
    .out_6(single_display_mirrored_5_out_6));
  set_cards set_cards_1 (
    .in_1(in_1), .out_2(d0), .out_3(d1), .out_4(d2), .out_5(d3), .out_6(d4), .out_7(d5), .out_8(d6),
    .out_9(d7), .out_10(d8), .out_11(d9));
endmodule

module buttons (
  input  in_1,
  input  in_2,
  input  in_3,
  input  in_4,
  input  in_5,
  input  in_6,
  input  in_7,
  input  in_8,
  input  in_9,
  input  in_10
);
endmodule

module set_cards (
  input  in_1,
  output [8:0] out_2,
  output [8:0] out_3,
  output [8:0] out_4,
  output [8:0] out_5,
  output [8:0] out_6,
  output [8:0] out_7,
  output [8:0] out_8,
  output [8:0] out_9,
  output [8:0] out_10,
  output [8:0] out_11
);

  wire clk, clock_2_out, end_b, eq0, eq1, eq2, eq3, eq4, eq5, eq6, eq7, eq8, eq9, n0, n1, n2, n3, n4, n5, n6,
       n7, n8, n9, not_1_out, r0, r1, r2, r3, r4, r5, r6, r7, r8, r9, start;
  wire [3:0] count, randN;
  wire [8:0] c0, c1, c2, c3, c4, d0, d1, d2, d3, d4, d5, d6, d7, d8, d9, multiplexer_1_out;

  Clock clock_1 (.out(clk));
  deck deck_1 (.set(in_1), .out_2(c0), .out_3(c1), .out_4(c2), .out_5(c3), .out_6(c4), .out_7(end_b));
  Demultiplexer #(.select(4)) demultiplexer_1 (
    .out1(n0), .out2(n1), .out3(n2), .out4(n3), .out5(n4), .out6(n5), .out7(n6), .out8(n7), .out9(n8),
    .out10(n9), .in(start), .sel(randN));  // open: out0, out11, out12, out13, out14, out15
  Multiplexer #(.select(4), .width(9)) multiplexer_1 (
    .in1(c0), .in2(c0), .in3(c1), .in4(c1), .in5(c2), .in6(c2), .in7(c3), .in8(c3), .in9(c4), .in10(c4),
    .out(multiplexer_1_out), .sel(count));  // open: in0, in11, in12, in13, in14, in15
  Comparator #(.width(9)) comparator_1 (.a(out_2), .b({9{1'b0}}), .eq(eq0));  // open: gt, lt
  Comparator #(.width(9)) comparator_2 (.a(out_4), .b({9{1'b0}}), .eq(eq2));  // open: gt, lt
  Comparator #(.width(9)) comparator_3 (.a(out_6), .b({9{1'b0}}), .eq(eq4));  // open: gt, lt
  Comparator #(.width(9)) comparator_4 (.a(out_8), .b({9{1'b0}}), .eq(eq6));  // open: gt, lt
  Comparator #(.width(9)) comparator_5 (.a(out_10), .b({9{1'b0}}), .eq(eq8));  // open: gt, lt
  Random #(.width(4)) random_1 (.next(start), .clk(clock_2_out), .out(randN));  // open: clr
  Clock clock_2 (.out(clock_2_out));
  Demultiplexer #(.select(4), .width(9)) demultiplexer_2 (
    .out1(d0), .out2(d1), .out3(d2), .out4(d3), .out5(d4), .out6(d5), .out7(d6), .out8(d7), .out9(d8),
    .out10(d9), .in(multiplexer_1_out), .sel(randN));  // open: out0, out11, out12, out13, out14, out15
  and and_1 (r0, n0, eq0);
  and and_2 (r2, n2, eq2);
  and and_3 (r0, n4, eq4);
  and and_4 (r0, n6, eq6);
  and and_5 (r0, n8, eq8);
  Comparator #(.width(9)) comparator_6 (.a(out_3), .b({9{1'b0}}), .eq(eq1));  // open: gt, lt
  Comparator #(.width(9)) comparator_7 (.a(out_5), .b({9{1'b0}}), .eq(eq3));  // open: gt, lt
  Comparator #(.width(9)) comparator_8 (.a(out_7), .b({9{1'b0}}), .eq(eq5));  // open: gt, lt
  Comparator #(.width(9)) comparator_9 (.a(out_9), .b({9{1'b0}}), .eq(eq7));  // open: gt, lt
  Comparator #(.width(9)) comparator_10 (.a(out_11), .b({9{1'b0}}), .eq(eq9));  // open: gt, lt
  and and_6 (r1, n1, eq1);
  and and_7 (r3, n3, eq3);
  and and_8 (r5, n5, eq5);
  and and_9 (r7, n7, eq7);
  and and_10 (r9, n9, eq9);
  Counter #(.max('ha), .width(4)) counter_1 (
    .clr(not_1_out), .count(start), .clk(clk), .Q(count));  // open: load, up, D, carry
  not not_1 (not_1_out, end_b);
  Register #(.width(9)) register_1 (.D(d0), .en(r0), .clk(clk), .Q(out_2));  // open: clr
  Register #(.width(9)) register_2 (.D(d2), .en(r2), .clk(clk), .Q(out_4));  // open: clr
  Register #(.width(9)) register_3 (.D(d4), .en(r4), .clk(clk), .Q(out_6));  // open: clr
  Register #(.width(9)) register_4 (.D(d6), .en(r6), .clk(clk), .Q(out_8));  // open: clr
  Register #(.width(9)) register_5 (.D(d8), .en(r8), .clk(clk), .Q(out_10));  // open: clr
  Register #(.width(9)) register_6 (.D(d1), .en(r1), .clk(clk), .Q(out_3));  // open: clr
  Register #(.width(9)) register_7 (.D(d3), .en(r3), .clk(clk), .Q(out_5));  // open: clr
  Register #(.width(9)) register_8 (.D(d5), .en(r5), .clk(clk), .Q(out_7));  // open: clr
  Register #(.width(9)) register_9 (.D(d7), .en(r7), .clk(clk), .Q(out_9));  // open: clr
  Register #(.width(9)) register_10 (.D(d9), .en(r9), .clk(clk), .Q(out_11));  // open: clr
  and and_11 (start, eq0, eq1, eq2, eq3, eq4, end_b, eq0, eq1, eq2, eq3, eq4);

  // Other names for the same wires on the sheet: q0[8:0] = out_2; q1[8:0] = out_3; q2[8:0] = out_4; q3[8:0] = out_5;
  //   q4[8:0] = out_6; q5[8:0] = out_7; q6[8:0] = out_8; q7[8:0] = out_9; q8[8:0] = out_10; q9[8:0] = out_11
endmodule

module deck (
  input  set,
  output [8:0] out_2,
  output [8:0] out_3,
  output [8:0] out_4,
  output [8:0] out_5,
  output [8:0] out_6,
  output out_7
);

  wire and_1_out, clock_1_out, clock_2_out, clock_3_out, decoder_1_out1, decoder_1_out2, decoder_1_out3,
       decoder_1_out4, decoder_1_out5, not_1_out, not_2_out;
  wire [2:0] counter_1_q;
  wire [8:0] demultiplexer_1_out1, demultiplexer_1_out2, demultiplexer_1_out3, demultiplexer_1_out4,
       demultiplexer_1_out5, random_1_out;

  and and_1 (and_1_out, not_2_out, set);
  not not_1 (not_1_out, set);
  Counter #(.max('h5), .width(3)) counter_1 (
    .count(and_1_out), .Q(counter_1_q), .carry(out_7), .clk(clock_1_out), .clr(not_1_out));  // open: load, D, up
  Clock clock_1 (.out(clock_1_out));
  Random #(.width(9)) random_1 (.next(not_2_out), .clk(clock_2_out), .out(random_1_out));  // open: clr
  not not_2 (not_2_out, out_7);
  Clock clock_2 (.out(clock_2_out));
  Demultiplexer #(.select(3), .width(9)) demultiplexer_1 (
    .out1(demultiplexer_1_out1), .out2(demultiplexer_1_out2), .out3(demultiplexer_1_out3),
    .out4(demultiplexer_1_out4), .out5(demultiplexer_1_out5), .in(random_1_out), .sel(counter_1_q));  // open: out0, out6, out7
  Decoder #(.select(3)) decoder_1 (
    .out1(decoder_1_out1), .out2(decoder_1_out2), .out3(decoder_1_out3), .out4(decoder_1_out4),
    .out5(decoder_1_out5), .sel(counter_1_q));  // open: out0, out6, out7, en
  Clock clock_3 (.out(clock_3_out));
  Register #(.width(9)) register_1 (
    .D(demultiplexer_1_out1), .en(decoder_1_out1), .clk(clock_3_out), .Q(out_2));  // open: clr
  Register #(.width(9)) register_2 (
    .D(demultiplexer_1_out2), .en(decoder_1_out2), .clk(clock_3_out), .Q(out_3));  // open: clr
  Register #(.width(9)) register_3 (
    .D(demultiplexer_1_out3), .en(decoder_1_out3), .clk(clock_3_out), .Q(out_4));  // open: clr
  Register #(.width(9)) register_4 (
    .D(demultiplexer_1_out4), .en(decoder_1_out4), .clk(clock_3_out), .Q(out_5));  // open: clr
  Register #(.width(9)) register_5 (
    .D(demultiplexer_1_out5), .en(decoder_1_out5), .clk(clock_3_out), .Q(out_6));  // open: clr
endmodule

// _
module single_display (
  input  [8:0] in_1,
  output [4:0] out_2,
  output [4:0] out_3,
  output [4:0] out_4,
  output [4:0] out_5,
  output [4:0] out_6
);

  wire [4:0] bit_extender_1_out, bit_extender_2_out, bit_extender_3_out;

  assign bit_extender_1_out = {{2{1'b0}}, in_1[2:0]};  // Bit_Extender bit_extender_1
  assign bit_extender_2_out = {{2{1'b0}}, in_1[5:3]};  // Bit_Extender bit_extender_2
  assign bit_extender_3_out = {{2{1'b0}}, in_1[8:6]};  // Bit_Extender bit_extender_3
  Shifter #(.width(5)) shifter_1 (.in(bit_extender_1_out), .\dist (3'b001), .out(out_3));
  Shifter #(.width(5)) shifter_2 (.in(bit_extender_2_out), .\dist (3'b001), .out(out_4));
  Shifter #(.width(5)) shifter_3 (.in(bit_extender_3_out), .\dist (3'b001), .out(out_5));

  assign out_2 = {5{1'b0}};
  assign out_6 = {5{1'b0}};
endmodule

// __
module single_display_mirrored (
  input  [8:0] in_1,
  output [4:0] out_2,
  output [4:0] out_3,
  output [4:0] out_4,
  output [4:0] out_5,
  output [4:0] out_6
);

  wire [4:0] bit_extender_1_out, bit_extender_2_out, bit_extender_3_out;

  assign bit_extender_1_out = {{2{1'b0}}, in_1[2:0]};  // Bit_Extender bit_extender_1
  assign bit_extender_2_out = {{2{1'b0}}, in_1[5:3]};  // Bit_Extender bit_extender_2
  assign bit_extender_3_out = {{2{1'b0}}, in_1[8:6]};  // Bit_Extender bit_extender_3
  Shifter #(.width(5)) shifter_1 (.in(bit_extender_1_out), .\dist (3'b001), .out(out_5));
  Shifter #(.width(5)) shifter_2 (.in(bit_extender_2_out), .\dist (3'b001), .out(out_4));
  Shifter #(.width(5)) shifter_3 (.in(bit_extender_3_out), .\dist (3'b001), .out(out_3));

  assign out_2 = {5{1'b0}};
  assign out_6 = {5{1'b0}};
endmodule
